// Logisim project counter.circ as structural Verilog: 2 circuits, main circuit main
module main (
  input  x,
  output _0,
  output _1,
  output _2,
  output _3
);

  wire _0_q, _1_q, _2_q, _3_q, clock_1_out, combinational_1_j0, combinational_1_j1, combinational_1_j2,
       combinational_1_j3, combinational_1_k0, combinational_1_k1, combinational_1_k2, combinational_1_k3;

  combinational combinational_1 (
    .x(x), .p0(_0_q), .p1(_1_q), .p2(_2_q), .p3(_3_q), .z0(_0), .z1(_1), .z2(_2), .z3(_3),
    .J0(combinational_1_j0), .K0(combinational_1_k0), .J1(combinational_1_j1), .K1(combinational_1_k1),
    .J2(combinational_1_j2), .K2(combinational_1_k2), .J3(combinational_1_j3), .K3(combinational_1_k3));
  Clock clock_1 (.out(clock_1_out));
  J_K_Flip_Flop u__0 (
    .J(combinational_1_j0), .clk(clock_1_out), .K(combinational_1_k0), .Q(_0_q));  // open: Qn, preset, en, reset
  J_K_Flip_Flop u__1 (
    .J(combinational_1_j1), .clk(clock_1_out), .K(combinational_1_k1), .Q(_1_q));  // open: Qn, preset, en, reset
  J_K_Flip_Flop u__2 (
    .J(combinational_1_j2), .clk(clock_1_out), .K(combinational_1_k2), .Q(_2_q));  // open: Qn, preset, en, reset
  J_K_Flip_Flop u__3 (
    .J(combinational_1_j3), .clk(clock_1_out), .K(combinational_1_k3), .Q(_3_q));  // open: Qn, preset, en, reset

  // Notes on the sheet:
  //   0
  //   1
  //   2
  //   3
endmodule

module combinational (
  input  x,
  input  p0,
  input  p1,
  input  p2,
  input  p3,
  output z0,
  output z1,
  output z2,
  output z3,
  output J0,
  output K0,
  output J1,
  output K1,
  output J2,
  output K2,
  output J3,
  output K3
);

  and and_1 (J0, x, ~p3);  // AND_Gate
  and and_2 (J1, x, p0);
  and and_3 (J2, J1, p1);
  and and_4 (J3, J2, p2);

  assign K0 = x;
  assign K1 = J1;
  assign K2 = J2;
  assign K3 = x;
  assign z0 = 1'b1;
  assign z1 = 1'b1;
  assign z2 = 1'b1;
  assign z3 = 1'b1;
endmodule
