// Logisim project Elevator.circ as structural Verilog: 1 circuit, main circuit main
module main (
  input  Up,
  input  Down
);

  wire clock_1_out, D0_q, D0_qn, D1_q, D1_qn, D2_q, D2_qn, D3_q, D3_qn;

  Clock clock_1 (.out(clock_1_out));
  D_Flip_Flop D0 (.clk(clock_1_out), .Q(D0_q), .Qn(D0_qn));  // open: D, preset, en, reset
  D_Flip_Flop D1 (.clk(clock_1_out), .Q(D1_q), .Qn(D1_qn));  // open: D, preset, en, reset
  D_Flip_Flop D2 (.clk(clock_1_out), .Q(D2_q), .Qn(D2_qn));  // open: D, preset, en, reset
  D_Flip_Flop D3 (.clk(clock_1_out), .Q(D3_q), .Qn(D3_qn));  // open: D, preset, en, reset

  // Notes on the sheet:
  //   P0
  //   P1
  //   P2
  //   P3
  //   P0'
  //   P1'
  //   P2'
  //   P3'
endmodule
